# Fritzing sketch Knock (saved by Fritzing 0.9.3b)
breadboards: 1

parts:
  부품1 = Arduino Uno (Rev3)
  J1 = Piezo Speaker
  R1 = Resistor [tolerance=±5% resistance=1M package="1206 [SMD]"]

nets:
  N1: 부품1.A0, J1.pin2, R1.Pin_1
  N2: 부품1.GND, J1.pin1, R1.Pin_0
