# Fritzing sketch bargraph (saved by Fritzing 0.9.3b)
breadboards: 1

parts:
  Arduino = Arduino Uno (Rev3)
  R1 = Resistor [tolerance=±5% resistance=220 package=THT]
  R2 = Resistor [tolerance=±5% resistance=220 package=THT]
  R3 = Resistor [tolerance=±5% resistance=220 package=THT]
  R4 = Resistor [tolerance=±5% resistance=220 package=THT]
  R5 = Resistor [tolerance=±5% resistance=220 package=THT]
  R6 = Resistor [tolerance=±5% resistance=220 package=THT]
  R7 = Resistor [tolerance=±5% resistance=220 package=THT]
  R9 = Resistor [tolerance=±5% resistance=220 package=THT]
  R10 = Resistor [tolerance=±5% resistance=220 package=THT]
  R8 = Resistor [tolerance=±5% resistance=220 package=THT]
  LED_01 = smd LED [color="Red (660nm)" package="0805 [SMD]"]
  LED_02 = smd LED [color="Red (660nm)" package="0805 [SMD]"]
  LED_03 = smd LED [color="Orange (620nm)" package="0805 [SMD]"]
  LED_04 = smd LED [color="Orange (620nm)" package="0805 [SMD]"]
  LED_05 = smd LED [color="Orange (620nm)" package="0805 [SMD]"]
  LED_06 = smd LED [color="Orange (620nm)" package="0805 [SMD]"]
  LED_07 = smd LED [color="Green (570nm)" package="0805 [SMD]"]
  LED_08 = smd LED [color="Green (570nm)" package="0805 [SMD]"]
  LED_09 = smd LED [color="Green (570nm)" package="0805 [SMD]"]
  LED_10 = smd LED [color="Green (570nm)" package="0805 [SMD]"]

nets:
  N1: Arduino.D8, LED_07.anode
  N2: Arduino.D9_PWM, LED_08.anode
  N3: Arduino.D10_PWM/SS, R9.Pin_0, LED_09.cathode, LED_09.anode
  N4: Arduino.D11_PWM/MOSI, LED_10.anode
  N5: Arduino.GND, R1.Pin_1, R2.Pin_1, R3.Pin_1, R4.Pin_1, R5.Pin_1, R6.Pin_1, R7.Pin_1, R9.Pin_1, R10.Pin_1, R8.Pin_1
  N6: Arduino.D2, LED_01.anode
  N7: Arduino.D3_PWM, LED_02.anode
  N8: Arduino.D4, LED_03.anode
  N9: Arduino.D5_PWM, LED_04.anode
  N10: Arduino.D6_PWM, LED_05.anode
  N11: Arduino.D7, LED_06.anode
  N12: R1.Pin_0, LED_01.cathode
  N13: R2.Pin_0, LED_02.cathode
  N14: R3.Pin_0, LED_03.cathode
  N15: R4.Pin_0, LED_04.cathode
  N16: R5.Pin_0, LED_05.cathode
  N17: R6.Pin_0, LED_06.cathode
  N18: R7.Pin_0, LED_07.cathode
  N19: R10.Pin_0, LED_10.cathode
  N20: R8.Pin_0, LED_08.cathode
