# Fritzing sketch bargraph2 (saved by Fritzing 0.9.3b)
breadboards: 1

parts:
  Arduino = Arduino Uno (Rev3)
  R1 = Resistor [tolerance=±5% resistance=220 package="0805 [SMD]"]
  R2 = Resistor [tolerance=±5% resistance=220 package="0805 [SMD]"]
  R3 = Resistor [tolerance=±5% resistance=220 package="0805 [SMD]"]
  R4 = Resistor [tolerance=±5% resistance=220 package="0805 [SMD]"]
  R5 = Resistor [tolerance=±5% resistance=220 package="0805 [SMD]"]
  R6 = Resistor [tolerance=±5% resistance=220 package="0805 [SMD]"]
  R7 = Resistor [tolerance=±5% resistance=220 package="0805 [SMD]"]
  R8 = Resistor [tolerance=±5% resistance=220 package="0805 [SMD]"]
  R9 = Resistor [tolerance=±5% resistance=220 package="0805 [SMD]"]
  R10 = Resistor [tolerance=±5% resistance=220 package="0805 [SMD]"]
  LED1 = smd LED [color="Green (570nm)" package="1206 [SMD]"]
  LED2 = smd LED [color="Green (570nm)" package="1206 [SMD]"]
  LED3 = smd LED [color="Green (570nm)" package="1206 [SMD]"]
  LED4 = smd LED [color="Green (570nm)" package="1206 [SMD]"]
  LED5 = smd LED [color="Yellow (595nm)" package="1206 [SMD]"]
  LED6 = smd LED [color="Yellow (595nm)" package="1206 [SMD]"]
  LED7 = smd LED [color="Yellow (595nm)" package="1206 [SMD]"]
  LED8 = smd LED [color="Yellow (595nm)" package="1206 [SMD]"]
  LED9 = smd LED [color="Red (633nm)" package="1206 [SMD]"]
  LED10 = smd LED [color="Red (633nm)" package="1206 [SMD]"]
  U1 = POT [package=pot_mammoth]  # not connected

nets:
  N1: Arduino.D8, LED4.cathode
  N2: Arduino.D9_PWM, LED3.cathode
  N3: Arduino.D10_PWM/SS, LED2.cathode
  N4: Arduino.D11_PWM/MOSI, LED1.cathode
  N5: Arduino.GND, R2.Pin_1, R3.Pin_1, R5.Pin_1, R6.Pin_1, R8.Pin_1, R9.Pin_1
  N6: Arduino.D2, LED10.cathode
  N7: Arduino.D3_PWM, LED9.cathode
  N8: Arduino.D4, LED8.cathode
  N9: Arduino.D5_PWM, LED7.cathode
  N10: Arduino.D6_PWM, LED6.cathode
  N11: Arduino.D7, LED5.cathode
  N12: R1.Pin_0, LED1.anode
  N13: R2.Pin_0, LED2.anode
  N14: R3.Pin_0, LED3.anode
  N15: R4.Pin_0, LED4.anode
  N16: R5.Pin_0, LED6.anode
  N17: R6.Pin_0, LED5.anode
  N18: R7.Pin_0, LED7.anode
  N19: R8.Pin_0, LED8.anode
  N20: R9.Pin_0, LED9.anode
  N21: R10.Pin_0, LED10.anode
